# Fritzing sketch Midi_Out_Arduino (saved by Fritzing 0.9.10b)
breadboards: 1

parts:
  U1 = MIDI_CONN_FEMALE [package=din_5_female]  # not connected
  Part1 = Arduino Uno (Rev3) - ICSP
  R1 = Resistor [tolerance=±5% resistance=220 package="0603 [SMD]"]
  R2 = Resistor [tolerance=±5% resistance=220 package="0603 [SMD]"]

nets:
  N1: Part1.D1/TX, R1.Pin_1
  N2: Part1.5V, R2.Pin_1

notes:
  Pin5
  Front view
  Resistors 220 Ohm
  Pin 4
  Front View
