# Fritzing sketch Midi_Out_PIco._with_logiclevelconv (saved by Fritzing 0.9.10b)
breadboards: 1

parts:
  U1 = MIDI_CONN_FEMALE [package=din_5_female]  # not connected
  R1 = Resistor [tolerance=±5% resistance=10 package="0603 [SMD]"]
  R2 = Resistor [tolerance=±5% resistance=33 package="0603 [SMD]"]
  Mod1 = Raspberry Pi Pico
  Part1 = I2C level shifter bidirectional

nets:
  N1: R1.Pin_1, Part1.HV1
  N2: R2.Pin_1, Mod1.pin_39, Part1.HV
  N3: Mod1.pin_6, Part1.LV1
  N4: Mod1.pin_36, Part1.LV
  N5: Mod1.pin_38, Mod1.pin_42, Part1.GND

notes:
  Pin5
  Front view
  220 Ohm
  Pin6
  Pin 4
  Front View
  220 Ohm
  Plus

custom parts:
  Raspberry Pi Pico: Raspberry Pi Pico. Based around the RP2040 microcontroller the Pico is a low cost microcontroller device bringing Raspberry Pi quality, cost, and easy of use to the microcontroller space. Jan 2021, Split part in to two versions: tht (this one) and SMD. This one will drill holes for a .1 in header in pcb to allow plugging in the module as well as providing pads to solder the module to the top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
